# Fritzing sketch Untitled Sketch (saved by Fritzing 0.7.0b)
breadboards: 1

parts:
  R1 = Resistor [tolerance=±5% resistance=220 package=THT]
  U1 = NodeMCU V1.0
  LED1 = LED - 5mm [color="Red (633nm)" package="5 mm [THT]"]
  LED2 = LED - 5mm [color="Red (633nm)" package="5 mm [THT]"]
  LED3 = LED - 5mm [color="Red (633nm)" package="5 mm [THT]"]
  R2 = Resistor [tolerance=±5% resistance=220 package=THT]
  R3 = Resistor [tolerance=±5% resistance=220 package=THT]
  J4 = Screw terminal - 2 pins [package=THT]
  HLK-PM1 = HLK-PM01
  J5 = Screw terminal - 2 pins [package=THT]
  J6 = Screw terminal - 2 pins [package=THT]
  J7 = Screw terminal - 2 pins [package=THT]
  J8 = Screw terminal - 2 pins [package=THT]
  SW1 = Pushbutton [package="[THT]"]
  R4 = Resistor [tolerance=±5% resistance=220 package=THT]
  Fuse1 = Fuse with Handler [part_number=Htc-15m]

nets:
  N1: R1.Pin_0, U1.D2
  N2: R1.Pin_1, LED3.anode
  N3: U1.D3, R2.Pin_0
  N4: U1.GND, LED1.cathode, LED2.cathode, LED3.cathode, HLK-PM1.-Vo, J5.pin1, J6.pin2, J7.pin2, J8.pin2, R4.Pin_1
  N5: U1.D5, R3.Pin_0
  N6: U1.D6, SW1.Pin_1, SW1.Pin_2, R4.Pin_0
  N7: LED1.anode, R3.Pin_1
  N8: LED2.anode, R2.Pin_1
  N9: J4.pin1, Fuse1.Connector1
  N10: J4.pin2, HLK-PM1.AC#1
  N11: HLK-PM1.AC#0, Fuse1.Connector2
  N12: HLK-PM1.+Vo, J5.pin2, SW1.Pin_3, SW1.Pin_4

notes:
  By Thanakrit

custom parts:
  NodeMCU V1.0: ESP8266 based NodeMCU
